// Logisim project my_full_adder.circ as structural Verilog
module one_bit_full_adder (
  input  a,
  input  b,
  input  c,
  output C_out,
  output s
);

  wire and_1_out, and_2_out, and_3_out, and_4_out, and_5_out, and_6_out, and_7_out, not_1_out, not_2_out,
       not_3_out;

  not not_1 (not_1_out, a);
  not not_2 (not_2_out, b);
  not not_3 (not_3_out, c);
  and and_1 (and_1_out, b, c);
  and and_2 (and_2_out, a, c);
  or or_1 (C_out, and_1_out, and_2_out, and_3_out);
  and and_3 (and_3_out, a, b);
  and and_4 (and_4_out, not_1_out, not_2_out, c);
  and and_5 (and_5_out, not_1_out, b, not_3_out);
  and and_6 (and_6_out, a, not_2_out, not_3_out);
  and and_7 (and_7_out, a, b, c);
  or or_2 (s, and_4_out, and_5_out, and_6_out, and_7_out);
endmodule

module four_bit_adder (
  input  [3:0] A,
  input  [3:0] B,
  input  in_3,
  output cout,
  output [3:0] s
);

  wire one_bit_full_adder_2_c_out, one_bit_full_adder_3_c_out, one_bit_full_adder_4_c_out;

  one_bit_full_adder one_bit_full_adder_1 (.a(A[3]), .b(B[3]), .c(one_bit_full_adder_2_c_out), .C_out(cout), .s(s[3]));
  one_bit_full_adder one_bit_full_adder_2 (
    .a(A[2]), .b(B[2]), .c(one_bit_full_adder_3_c_out), .C_out(one_bit_full_adder_2_c_out), .s(s[2]));
  one_bit_full_adder one_bit_full_adder_3 (
    .a(A[1]), .b(B[1]), .c(one_bit_full_adder_4_c_out), .C_out(one_bit_full_adder_3_c_out), .s(s[1]));
  one_bit_full_adder one_bit_full_adder_4 (.a(A[0]), .b(B[0]), .c(in_3), .C_out(one_bit_full_adder_4_c_out), .s(s[0]));
endmodule
