// Logisim project my_mux.circ as structural Verilog
module two_by_one_mux (
  input  a,
  input  s,
  input  b,
  output f
);

  wire and_1_out, and_2_out, not_1_out;

  not not_1 (not_1_out, s);
  and and_1 (and_1_out, a, not_1_out);
  and and_2 (and_2_out, s, b);
  nor nor_1 (f, and_1_out, and_2_out);
endmodule

module four_by_one_mux (
  input  i0,
  input  i1,
  input  i2,
  input  i3,
  input  s0,
  input  s1,
  output f
);

  wire and_1_out, and_2_out, and_3_out, and_4_out, not_1_out, not_2_out;

  not not_1 (not_1_out, s0);
  not not_2 (not_2_out, s1);
  and and_1 (and_1_out, i3, s0, s1);
  and and_2 (and_2_out, i2, not_1_out, s1);
  and and_3 (and_3_out, i1, s0, not_2_out);
  and and_4 (and_4_out, i0, not_1_out, not_2_out);
  or or_1 (f, and_1_out, and_2_out, and_3_out, and_4_out);
endmodule

module eight_by_one_mux (
  input  i0,
  input  i1,
  input  i2,
  input  i3,
  input  i4,
  input  i5,
  input  i6,
  input  i7,
  input  s0,
  input  s1,
  input  s2,
  output f
);

  wire and_1_out, and_2_out, and_3_out, and_4_out, and_5_out, and_6_out, and_7_out, and_8_out, not_1_out,
       not_2_out, not_3_out, not_4_out, not_5_out, not_6_out, not_7_out, not_8_out, not_9_out, not_10_out,
       not_11_out;

  not not_1 (not_1_out, i0);
  not not_2 (not_2_out, i1);
  not not_3 (not_3_out, i2);
  not not_4 (not_4_out, i3);
  not not_5 (not_5_out, i4);
  not not_6 (not_6_out, i5);
  not not_7 (not_7_out, i6);
  not not_8 (not_8_out, s0);
  not not_9 (not_9_out, i7);
  not not_10 (not_10_out, s1);
  not not_11 (not_11_out, s2);
  and and_1 (and_1_out, s0, not_9_out, s1, s2);
  and and_2 (and_2_out, not_7_out, s0, not_10_out, s2);
  and and_3 (and_3_out, not_6_out, s0, s1, not_11_out);
  and and_4 (and_4_out, not_4_out, not_8_out, s1, s2);
  and and_5 (and_5_out, not_1_out, not_8_out, not_10_out, not_11_out);
  and and_6 (and_6_out, not_5_out, s0, not_10_out, not_11_out);
  and and_7 (and_7_out, not_3_out, not_8_out, not_10_out, s2);
  and and_8 (and_8_out, not_2_out, not_8_out, s1, not_11_out);
  or or_1 (f, and_1_out, and_2_out, and_3_out, and_4_out, and_5_out, and_6_out, and_7_out, and_8_out);
endmodule

module sixteen_by_one_mux (
  input  i0,
  input  i1,
  input  i2,
  input  i3,
  input  i4,
  input  i5,
  input  i6,
  input  i7,
  input  i8,
  input  i9,
  input  i10,
  input  i11,
  input  b,
  input  a,
  input  i12,
  input  i13,
  input  i14,
  input  i15,
  input  d,
  input  c,
  output f
);

  wire four_by_one_mux_1_f, four_by_one_mux_2_f, four_by_one_mux_3_f, four_by_one_mux_4_f;

  four_by_one_mux four_by_one_mux_1 (.i0(i0), .i1(i1), .i2(i2), .i3(i3), .s0(d), .s1(c), .f(four_by_one_mux_1_f));
  four_by_one_mux four_by_one_mux_2 (.i0(i4), .i1(i5), .i2(i6), .i3(i7), .s0(d), .s1(c), .f(four_by_one_mux_2_f));
  four_by_one_mux four_by_one_mux_3 (.i0(i8), .i1(i9), .i2(i10), .i3(i11), .s0(d), .s1(c), .f(four_by_one_mux_3_f));
  four_by_one_mux four_by_one_mux_4 (.i0(i12), .i1(i13), .i2(i14), .i3(i15), .s0(d), .s1(c), .f(four_by_one_mux_4_f));
  four_by_one_mux four_by_one_mux_5 (
    .i0(four_by_one_mux_1_f), .i1(four_by_one_mux_2_f), .i2(four_by_one_mux_3_f), .i3(four_by_one_mux_4_f),
    .s0(b), .s1(a), .f(f));
endmodule

module sixteen_by_one_mux2 (
  input  in0,
  input  in1,
  input  in2,
  input  in3,
  input  in4,
  input  in5,
  input  in6,
  input  in7,
  input  f,
  input  in8,
  input  in9,
  input  in10,
  input  in11,
  input  in12,
  input  s3,
  input  in13,
  input  in14,
  input  in15,
  input  s0,
  input  s1,
  input  s2
);

  wire eight_by_one_mux_1_f, eight_by_one_mux_2_f;

  eight_by_one_mux eight_by_one_mux_1 (
    .i0(in0), .i1(in1), .i2(in2), .i3(in3), .i4(in4), .i5(in5), .i6(in6), .i7(in7), .s0(s0), .s1(s1),
    .s2(s2), .f(eight_by_one_mux_1_f));
  eight_by_one_mux eight_by_one_mux_2 (
    .i0(in8), .i1(in9), .i2(in10), .i3(in11), .i4(in12), .i5(in13), .i6(in14), .i7(in15), .s0(s0), .s1(s1),
    .s2(s2), .f(eight_by_one_mux_2_f));
  two_by_one_mux two_by_one_mux_1 (.a(eight_by_one_mux_1_f), .s(s3), .b(eight_by_one_mux_2_f), .f(f));
endmodule
