// Logisim project my_xor.circ as structural Verilog: 2 circuits, main circuit main
module main (
  input  in_1,
  input  in_2,
  output out_3
);

  myfirst_xor myfirst_xor_1 (.x(in_1), .y(in_2), .xXORy(out_3));
endmodule

module myfirst_xor (
  input  x,
  input  y,
  output xXORy
);

  wire and_1_out, and_2_out, not_1_out, not_2_out;

  not not_1 (not_1_out, x);
  not not_2 (not_2_out, y);
  and and_1 (and_1_out, not_1_out, y);
  and and_2 (and_2_out, x, not_2_out);
  nor nor_1 (xXORy, and_1_out, and_2_out);
endmodule
